// Logisim project uCode.circ as structural Verilog: 7 circuits, main circuit main
module main (
);

  wire [1:0] multiplexer_9_out_3, multiplexer_9_out_4;
  wire [2:0] multiplexer_9_out;
  wire [3:0] multiplexer_9_out_2;
  wire [11:0] INSTR_q;
  wire [15:0] alu_1_o_data, bram_1_o_rdata, lifo_1_o_s0, lifo_se_1_o_s0, lifo_se_1_o_s1, multiplexer_1_out,
       multiplexer_2_out, multiplexer_3_out, multiplexer_4_out, multiplexer_5_out, multiplexer_6_out,
       multiplexer_7_out, multiplexer_8_out, PC_q, qmem_1_o_data, undriven;
  wire [15:11] multiplexer_9_out_5;
  wire [15:12] INSTR_q_2;

  Multiplexer #(.width(16)) multiplexer_1 (.in0(multiplexer_5_out), .in1(PC_q), .out(multiplexer_1_out));  // open: sel
  LIFO_se lifo_se_1 (
    .i_data(multiplexer_5_out), .i_se(multiplexer_9_out), .o_s0(lifo_se_1_o_s0), .o_s1(lifo_se_1_o_s1));  // open: i_clk
  LIFO lifo_1 (
    .i_data(multiplexer_1_out), .i_push(multiplexer_9_out_5[13]), .i_pull(multiplexer_9_out_5[12]),
    .o_s0(lifo_1_o_s0));  // open: i_clk
  Multiplexer #(.select(2), .width(16)) multiplexer_2 (
    .in0(lifo_se_1_o_s0), .in1(lifo_se_1_o_s1), .in2(lifo_1_o_s0), .in3({16{1'b0}}), .out(multiplexer_2_out),
    .sel(multiplexer_9_out_3));
  Multiplexer #(.select(2), .width(16)) multiplexer_3 (
    .in0(lifo_se_1_o_s0), .in1(16'h1), .in2(16'h8000), .in3({16{1'b1}}), .out(multiplexer_3_out),
    .sel(multiplexer_9_out_4));
  ALU alu_1 (
    .i_arg0(multiplexer_2_out), .i_arg1(multiplexer_3_out), .i_op(multiplexer_9_out_2), .o_data(alu_1_o_data));  // open: i_clk
  Multiplexer #(.width(16)) multiplexer_4 (
    .in0(bram_1_o_rdata), .in1(multiplexer_6_out), .out(multiplexer_4_out));  // open: sel
  Multiplexer #(.width(16)) multiplexer_5 (
    .in0(alu_1_o_data), .in1(multiplexer_4_out), .out(multiplexer_5_out));  // open: sel
  Multiplexer #(.width(16)) multiplexer_6 (.in0(undriven), .in1(qmem_1_o_data), .out(multiplexer_6_out));  // open: sel
  Multiplexer #(.width(16)) multiplexer_7 (.in0(lifo_se_1_o_s0), .in1(PC_q), .out(multiplexer_7_out));  // open: sel
  Register #(.width(16)) PC (.D(multiplexer_8_out), .Q(PC_q));  // open: en, clk, clr
  Multiplexer #(.width(16)) multiplexer_8 (
    .in0({4'b0000, INSTR_q}), .in1(lifo_1_o_s0), .out(multiplexer_8_out), .sel(multiplexer_9_out_5[14]));
  Adder #(.width(16)) adder_1 (.b(PC_q));  // open: a, out, cin, cout
  QMEM qmem_1 (
    .i_addr(lifo_se_1_o_s1[11:0]), .i_data(lifo_se_1_o_s0), .o_data(qmem_1_o_data));  // open: i_wr, i_field, i_clk, i_cs_ram, i_cs_rom0, i_cs_rom1
  Register #(.width(16)) INSTR (.D(bram_1_o_rdata), .Q({INSTR_q_2, INSTR_q}));  // open: en, clk, clr
  BRAM bram_1 (
    .i_raddr(multiplexer_7_out[11:0]), .o_rdata(bram_1_o_rdata));  // open: i_rd_en, i_clk, i_wr_en, i_waddr, i_wdata
  Multiplexer #(.width(16)) multiplexer_9 (
    .in0({INSTR_q_2, INSTR_q}), .in1({16{1'b0}}),
    .out({multiplexer_9_out_5, multiplexer_9_out, multiplexer_9_out_3, multiplexer_9_out_4, multiplexer_9_out_2}),
    .sel(INSTR_q_2[15]));
  // NoConnect on multiplexer_9_out_5[15]
  // NoConnect on multiplexer_9_out_5[11]
  // NoConnect on INSTR_q[9]
  // NoConnect on INSTR_q[8]
  // NoConnect on INSTR_q[7]
  // NoConnect on INSTR_q[6]
  // NoConnect on INSTR_q[10]
  // NoConnect on INSTR_q[5]
  // NoConnect on INSTR_q[4]
  // NoConnect on INSTR_q[3]
  // NoConnect on INSTR_q[2]
  // NoConnect on INSTR_q[1]
  // NoConnect on INSTR_q[0]
endmodule

module QMEM (
  input  i_wr,
  input  [11:0] i_addr,
  input  [1:0] i_field,
  input  [15:0] i_data,
  input  i_clk,
  input  i_cs_ram,
  input  i_cs_rom0,
  input  i_cs_rom1,
  output [15:0] o_data
);

  wire and_1_out, and_2_out, and_3_out, and_4_out, not_1_out, not_2_out, not_3_out;
  wire [15:0] ram_1_dout;

  not not_1 (not_1_out, i_cs_ram);
  not not_2 (not_2_out, i_cs_rom0);
  not not_3 (not_3_out, i_cs_rom1);
  and and_1 (and_1_out, not_1_out, not_2_out, not_3_out);
  Multiplexer #(.width(16)) multiplexer_1 (.in0(ram_1_dout), .in1({16{1'b0}}), .out(o_data), .sel(and_1_out));
  RAM #(.addrWidth(14), .dataWidth(16)) ram_1 (
    .addr({i_addr, i_field}), .we(and_2_out), .oe(i_cs_ram), .clk(i_clk), .din(i_data), .dout(ram_1_dout));
  and and_2 (and_2_out, i_wr, i_cs_ram);
  RAM #(.addrWidth(14), .dataWidth(16)) ram_2 (
    .addr({i_addr, i_field}), .we(and_3_out), .oe(i_cs_rom0), .clk(i_clk), .din(i_data), .dout(ram_1_dout));
  and and_3 (and_3_out, i_wr, i_cs_rom0);
  and and_4 (and_4_out, i_wr, i_cs_rom1);
  RAM #(.addrWidth(14), .dataWidth(16)) ram_3 (
    .addr({i_addr, i_field}), .we(and_4_out), .oe(i_cs_rom1), .clk(i_clk), .din(i_data), .dout(ram_1_dout));
endmodule

module ALU (
  input  [15:0] i_arg0,
  input  [15:0] i_arg1,
  input  [3:0] i_op,
  input  i_clk,
  output [15:0] o_data
);

  wire [15:0] adder_1_out, and_1_out, multiplexer_1_out, multiplier_1_out, or_1_out, subtractor_1_out,
       undriven, xor_1_out;

  Register #(.width(16)) register_1 (.D(multiplexer_1_out), .en(1'b1), .clk(i_clk), .Q(o_data));  // open: clr
  Multiplexer #(.select(4), .width(16)) multiplexer_1 (
    .in0(i_arg0), .in1(adder_1_out), .in2(subtractor_1_out), .in3(multiplier_1_out), .in4(multiplier_1_out),
    .in5(and_1_out), .in6(or_1_out), .in7(xor_1_out), .in8({i_arg0[14:0], i_arg0[15]}),
    .in9({i_arg0[13:0], i_arg0[15:14]}), .in10({i_arg0[11:0], i_arg0[15:12]}),
    .in11({i_arg0[7:0], i_arg0[15:8]}), .in12({i_arg0[15], i_arg0[13:0], 1'b0}),
    .in13({i_arg0[15], i_arg0[12:0], 2'b00}), .in14({i_arg0[15], i_arg0[10:0], 4'b0000}), .in15(undriven),
    .out(multiplexer_1_out), .sel(i_op));
  // NoConnect on undriven
  Adder #(.width(16)) adder_1 (.a(i_arg0), .b(i_arg1), .out(adder_1_out), .cin(1'b0));  // open: cout
  Subtractor #(.width(16)) subtractor_1 (.a(i_arg0), .b(i_arg1), .out(subtractor_1_out), .bin(1'b0));  // open: bout
  Multiplier #(.width(16)) multiplier_1 (.a(i_arg0), .b(i_arg1), .out(multiplier_1_out));  // open: cin, cout
  assign and_1_out = i_arg1 & i_arg0;  // AND_Gate and_1, 16 bits wide
  assign or_1_out = i_arg1 | i_arg0;  // OR_Gate or_1, 16 bits wide
  assign xor_1_out = i_arg1 ^ i_arg0;  // XOR_Gate xor_1, 16 bits wide
endmodule

module LIFO_se (
  input  [2:0] i_se,
  input  [15:0] i_data,
  input  i_clk,
  output [15:0] o_s0,
  output [15:0] o_s1
);

  wire [15:0] multiplexer_1_out, multiplexer_2_out, multiplexer_3_out, multiplexer_4_out, multiplexer_5_out,
       multiplexer_6_out, multiplexer_7_out, multiplexer_8_out, multiplexer_9_out, multiplexer_10_out,
       multiplexer_11_out, multiplexer_12_out, multiplexer_13_out, multiplexer_14_out, multiplexer_15_out,
       multiplexer_16_out, register_3_q, register_4_q, register_5_q, register_6_q, register_7_q,
       register_8_q, register_9_q, register_10_q, register_11_q, register_12_q, register_13_q, register_14_q,
       register_15_q, register_16_q;

  Multiplexer #(.select(3), .width(16)) multiplexer_1 (
    .in0(o_s1), .in1(i_data), .in2(i_data), .in3(o_s1), .out(multiplexer_1_out), .sel(i_se));  // open: in4, in5, in6, in7
  Multiplexer #(.select(3), .width(16)) multiplexer_2 (
    .in0(register_3_q), .in1(o_s0), .in2(o_s1), .in3(o_s0), .out(multiplexer_2_out), .sel(i_se));  // open: in4, in5, in6, in7
  Multiplexer #(.select(3), .width(16)) multiplexer_3 (
    .in0(register_4_q), .in1(o_s1), .in2(register_3_q), .in3(register_3_q), .out(multiplexer_3_out),
    .sel(i_se));  // open: in4, in5, in6, in7
  Multiplexer #(.select(3), .width(16)) multiplexer_4 (
    .in0(register_5_q), .in1(register_3_q), .in2(register_4_q), .in3(register_4_q), .out(multiplexer_4_out),
    .sel(i_se));  // open: in4, in5, in6, in7
  Multiplexer #(.select(3), .width(16)) multiplexer_5 (
    .in0(register_6_q), .out(multiplexer_5_out), .sel(i_se));  // open: in1, in2, in3, in4, in5, in6, in7
  Multiplexer #(.select(3), .width(16)) multiplexer_6 (
    .in0(register_7_q), .out(multiplexer_6_out), .sel(i_se));  // open: in1, in2, in3, in4, in5, in6, in7
  Multiplexer #(.select(3), .width(16)) multiplexer_7 (
    .in0(register_8_q), .out(multiplexer_7_out), .sel(i_se));  // open: in1, in2, in3, in4, in5, in6, in7
  Multiplexer #(.select(3), .width(16)) multiplexer_8 (
    .in0(register_9_q), .out(multiplexer_8_out), .sel(i_se));  // open: in1, in2, in3, in4, in5, in6, in7
  Multiplexer #(.select(3), .width(16)) multiplexer_9 (
    .in0(register_10_q), .out(multiplexer_9_out), .sel(i_se));  // open: in1, in2, in3, in4, in5, in6, in7
  Multiplexer #(.select(3), .width(16)) multiplexer_10 (
    .in0(register_11_q), .out(multiplexer_10_out), .sel(i_se));  // open: in1, in2, in3, in4, in5, in6, in7
  Multiplexer #(.select(3), .width(16)) multiplexer_11 (
    .in0(register_12_q), .out(multiplexer_11_out), .sel(i_se));  // open: in1, in2, in3, in4, in5, in6, in7
  Multiplexer #(.select(3), .width(16)) multiplexer_12 (
    .in0(register_13_q), .out(multiplexer_12_out), .sel(i_se));  // open: in1, in2, in3, in4, in5, in6, in7
  Multiplexer #(.select(3), .width(16)) multiplexer_13 (
    .in0(register_14_q), .out(multiplexer_13_out), .sel(i_se));  // open: in1, in2, in3, in4, in5, in6, in7
  Multiplexer #(.select(3), .width(16)) multiplexer_14 (
    .in0(register_15_q), .out(multiplexer_14_out), .sel(i_se));  // open: in1, in2, in3, in4, in5, in6, in7
  Multiplexer #(.select(3), .width(16)) multiplexer_15 (
    .in0(register_16_q), .out(multiplexer_15_out), .sel(i_se));  // open: in1, in2, in3, in4, in5, in6, in7
  Multiplexer #(.select(3), .width(16)) multiplexer_16 (
    .in0({16{1'b0}}), .out(multiplexer_16_out), .sel(i_se));  // open: in1, in2, in3, in4, in5, in6, in7
  Register #(.width(16)) register_1 (.D(multiplexer_1_out), .clk(i_clk), .Q(o_s0));  // open: en, clr
  Register #(.width(16)) register_2 (.D(multiplexer_2_out), .clk(i_clk), .Q(o_s1));  // open: en, clr
  Register #(.width(16)) register_3 (.D(multiplexer_3_out), .clk(i_clk), .Q(register_3_q));  // open: en, clr
  Register #(.width(16)) register_4 (.D(multiplexer_4_out), .clk(i_clk), .Q(register_4_q));  // open: en, clr
  Register #(.width(16)) register_5 (.D(multiplexer_5_out), .clk(i_clk), .Q(register_5_q));  // open: en, clr
  Register #(.width(16)) register_6 (.D(multiplexer_6_out), .clk(i_clk), .Q(register_6_q));  // open: en, clr
  Register #(.width(16)) register_7 (.D(multiplexer_7_out), .clk(i_clk), .Q(register_7_q));  // open: en, clr
  Register #(.width(16)) register_8 (.D(multiplexer_8_out), .clk(i_clk), .Q(register_8_q));  // open: en, clr
  Register #(.width(16)) register_9 (.D(multiplexer_9_out), .clk(i_clk), .Q(register_9_q));  // open: en, clr
  Register #(.width(16)) register_10 (.D(multiplexer_10_out), .clk(i_clk), .Q(register_10_q));  // open: en, clr
  Register #(.width(16)) register_11 (.D(multiplexer_11_out), .clk(i_clk), .Q(register_11_q));  // open: en, clr
  Register #(.width(16)) register_12 (.D(multiplexer_12_out), .clk(i_clk), .Q(register_12_q));  // open: en, clr
  Register #(.width(16)) register_13 (.D(multiplexer_13_out), .clk(i_clk), .Q(register_13_q));  // open: en, clr
  Register #(.width(16)) register_14 (.D(multiplexer_14_out), .clk(i_clk), .Q(register_14_q));  // open: en, clr
  Register #(.width(16)) register_15 (.D(multiplexer_15_out), .Q(register_15_q));  // open: en, clk, clr
  Register #(.width(16)) register_16 (.D(multiplexer_16_out), .clk(i_clk), .Q(register_16_q));  // open: en, clr

  // Notes on the sheet:
  //   https://github.com/zarutian/uFork/blob/main/fpga/fomu/cpu/lifo.v
  //   s0
  //   s1
  //   s2
  //   s3
  //   s4
  //   s5
  //   s6
  //   s7
  //   s8
  //   s9
  //   sA
  //   sB
  //   sC
  //   sD
  //   sE
  //   sF
  //   TOS
  //   NOS
endmodule

module LIFO (
  input  [15:0] i_data,
  input  i_push,
  input  i_pull,
  input  i_clk,
  output [15:0] o_s0
);

  wire and_1_out, not_1_out, or_1_out;
  wire [3:0] counter_1_q;

  not not_1 (not_1_out, i_pull);
  or or_1 (or_1_out, i_push, i_push);
  and and_1 (and_1_out, not_1_out, i_push);
  Counter #(.max('hf), .width(4)) counter_1 (
    .up(and_1_out), .count(or_1_out), .clk(i_clk), .Q(counter_1_q));  // open: clr, load, D, carry
  RAM #(.addrWidth(4), .dataWidth(16)) ram_1 (
    .addr(counter_1_q), .oe(1'b1), .clk(i_clk), .din(i_data), .dout(o_s0));  // open: we
endmodule

module BRAM (
  input  i_rd_en,
  input  i_wr_en,
  input  [11:0] i_raddr,
  input  [11:0] i_waddr,
  input  [15:0] i_wdata,
  input  i_clk,
  output [15:0] o_rdata
);
endmodule

module PC (
  input  i_rst,
  input  i_load,
  input  i_cnt,
  input  i_clk,
  input  [15:0] i_pc,
  output [15:0] o_pc
);

  Counter #(.max('hffff), .width(16)) counter_1 (
    .clr(i_rst), .load(i_load), .up(1'b1), .count(i_cnt), .clk(i_clk), .D(i_pc), .Q(o_pc));  // open: carry
endmodule
